# Fritzing sketch contavoltas (saved by Fritzing 0.9.3b)
breadboards: 1

parts:
  Part1 = Arduino Nano (Rev3.0)
  S1 = Momentary Switch [package=ksa_sealed_tac_switch]
  LED1 = smd LED [color="Red (633nm)" package="1206 [SMD]"]
  LED2 = smd LED [color="Green (555nm)" package="1206 [SMD]"]
  LED3 = smd LED [color="Orange (605nm)" package="1206 [SMD]"]
  R1 = Resistor [tolerance=±5% resistance=10k package="0805 [SMD]"]
  R2 = Resistor [tolerance=±5% resistance=100 package="0805 [SMD]"]
  R3 = Resistor [tolerance=±5% resistance=100 package="0805 [SMD]"]
  R4 = Resistor [tolerance=±5% resistance=100 package="0805 [SMD]"]
  BUZZER1 = Piezo Speaker
  U1 = LCD-16X2 [package=lcd-16x2_noholes]
  RJ-1 = RJ-11 Connector with Breakout Board  # not connected

nets:
  N1: Part1.D2, U1.DB7
  N2: Part1.D3, U1.DB6
  N3: Part1.D4, U1.DB5
  N4: Part1.D5, U1.DB4
  N5: Part1.D6, U1.VO
  N6: Part1.D7, S1.1, R1.Pin_1
  N7: Part1.D8, R2.Pin_1
  N8: Part1.D9, R4.Pin_1
  N9: Part1.D10, R3.Pin_1
  N10: Part1.D11/MOSI, U1.E
  N11: Part1.D12/MISO, U1.RS
  GND: Part1.GND, LED1.cathode, LED2.cathode, LED3.cathode, R1.Pin_0, BUZZER1.pin1, U1.VSS, U1.R_W, U1.K
  5V: Part1.5V, S1.3, U1.VDD
  N12: Part1.3V3, U1.A
  N13: LED1.anode, R2.Pin_0
  N14: LED2.anode, R3.Pin_0
  N15: LED3.anode, R4.Pin_0

notes:
  Sara Aguado Couselo © 2019
